# Fritzing sketch board (saved by Fritzing 0.9.2b)
circuit board: 8.46667cm x 5.64444cm
breadboards: 1

parts:
  Q1 = NPN-Transistor [part_number=BC549 package="TO92 [THT]"]
  Part1 = Arduino Uno (Rev3)
  R1 = Photocell (LDR) [part_number=SFH235 package=THT]
  LED1 = LED - 5mm [color="Infrared (940nm)" package="5 mm [THT]"]
  R2 = Resistor [tolerance=±5% resistance=1M package=THT]
  R3 = Resistor [tolerance=±5% resistance=1M package=THT]

nets:
  N1: Q1.E, Part1.GND, LED1.cathode
  N2: Q1.B, R2.Pin_1
  N3: Q1.C, Part1.A0, R3.Pin_0
  N4: Part1.D3_PWM, LED1.anode
  N5: Part1.5V, R1.pin_1, R3.Pin_1
  N6: R1.pin_0, R2.Pin_0
